// Logisim project cache.circ as structural Verilog: 2 circuits, main circuit cache-entry
module main (
  input  [7:0] address,
  input  read_enable,
  input  [31:0] ROM_data_in,
  output [7:0] data_out,
  output [5:0] ROM_read_address,
  output ROM_read_enable
);

  wire and_1_out, and_2_out, and_3_out, and_4_out, cache_entry_1_miss, cache_entry_2_miss,
       cache_entry_3_miss, cache_entry_4_miss, decoder_1_out0, decoder_1_out1, decoder_1_out2, decoder_1_out3;
  wire [31:0] cache_entry_4_data_out, undriven;

  Decoder #(.select(2), .enable("false")) decoder_1 (
    .out0(decoder_1_out0), .out1(decoder_1_out1), .out2(decoder_1_out2), .out3(decoder_1_out3),
    .sel(address[3:2]));
  and and_1 (and_1_out, decoder_1_out0, read_enable);
  and and_2 (and_2_out, decoder_1_out1, read_enable);
  and and_3 (and_3_out, decoder_1_out2, read_enable);
  and and_4 (and_4_out, decoder_1_out3, read_enable);
  cache_entry cache_entry_1 (
    .tag(address[7:4]), .clock(and_1_out), .miss(cache_entry_1_miss));  // open: data_out, data_in
  cache_entry cache_entry_2 (
    .tag(address[7:4]), .clock(and_2_out), .miss(cache_entry_2_miss));  // open: data_out, data_in
  cache_entry cache_entry_3 (
    .tag(address[7:4]), .clock(and_3_out), .miss(cache_entry_3_miss));  // open: data_out, data_in
  cache_entry cache_entry_4 (
    .tag(address[7:4]), .clock(and_4_out), .data_out(cache_entry_4_data_out), .miss(cache_entry_4_miss),
    .data_in(undriven));
  cache_entry cache_entry_5 (
    .tag(address[7:4]), .clock(and_4_out), .data_out(cache_entry_4_data_out), .miss(cache_entry_4_miss),
    .data_in(undriven));
  Multiplexer #(.select(2), .enable("false")) multiplexer_1 (
    .in0(cache_entry_1_miss), .in1(cache_entry_2_miss), .in2(cache_entry_3_miss), .in3(cache_entry_4_miss),
    .out(ROM_read_enable), .sel(address[3:2]));
  Multiplexer #(.select(2), .width(8), .enable("false")) multiplexer_2 (
    .in0(ROM_data_in[7:0]), .in1(ROM_data_in[15:8]), .in2(ROM_data_in[23:16]), .in3(ROM_data_in[31:24]),
    .out(data_out), .sel(address[1:0]));

  assign ROM_read_address = address[7:2];

  // Notes on the sheet:
  //   ROM_read_enable: pull=down
  //   ROM_read_address: pull=down
  //   data_out: pull=down
  //   byte offset
  //   index
  //   tag
  //   00
  //   01
  //   10
  //   11
endmodule

module cache_entry (
  input  [31:0] data_in,
  input  [3:0] tag,
  input  clock,
  output [31:0] data_out,
  output miss
);

  wire comparator_1_eq, or_1_out, valid_q;
  wire [3:0] tag_q;

  Register #(.width(4)) u_tag (.D(tag), .en(miss), .Q(tag_q), .clk(clock));  // open: clr
  not not_1 (miss, comparator_1_eq);
  Comparator #(.width(4)) comparator_1 (.a(tag), .b(tag_q), .eq(comparator_1_eq));  // open: gt, lt
  Register #(.width(1)) valid (.D(or_1_out), .Q(valid_q), .clk(clock));  // open: en, clr
  or or_1 (or_1_out, valid_q, miss);
  Register #(.width(32)) data (.D(data_in), .en(miss), .Q(data_out), .clk(clock));  // open: clr
endmodule
